# Fritzing sketch mpu6050 (saved by Fritzing 0.9.3b)
breadboards: 1

parts:
  Part2 = InvenSense MPU6050
  Part1 = Arduino Mega 2560 (Rev3)

nets:
  VCC: Part2.VCC, Part1.5V
  GND: Part2.GND, Part1.GND
  N1: Part2.SCL, Part1.D21/SCL
  N2: Part2.SDA, Part1.D20/SDA
  N3: Part2.INT, Part1.D2_PWM
